// Logisim project Circuito Calculadora.circ as structural Verilog: 9 circuits, main circuit main
// q
module main (
  input  [11:0] in_1,
  input  [1:0] \Selector_de_función ,
  input  Invertir_entradas,
  input  [11:0] in_4,
  output [12:0] out_5
);

  wire Complemento_a_la_base_out_3, sumador_de_12_bits_1_overflow;
  wire [11:0] Complemento_a_la_base_out_2, demultiplexer_1_out0, demultiplexer_1_out2, demultiplexer_1_out3,
       demultiplexer_2_out0, demultiplexer_2_out1, demultiplexer_2_out3, multiplexer_1_out,
       multiplexer_2_out, multiplexer_3_out, multiplexer_4_out, multiplexer_5_out, sumador_de_12_bits_1_out_3;

  Multiplexer #(.width(12)) multiplexer_1 (
    .in0(in_1), .in1(in_4), .out(multiplexer_1_out), .sel(Invertir_entradas), .en(1'b1));
  Multiplexer #(.width(12)) multiplexer_2 (
    .in0(in_4), .in1(in_1), .out(multiplexer_2_out), .sel(Invertir_entradas), .en(1'b1));
  Demultiplexer #(.select(2), .width(12)) demultiplexer_1 (
    .out0(demultiplexer_1_out0), .out2(demultiplexer_1_out2), .out3(demultiplexer_1_out3),
    .in(multiplexer_2_out), .sel(\Selector_de_función ), .en(1'b1));  // open: out1
  Demultiplexer #(.select(2), .width(12)) demultiplexer_2 (
    .out0(demultiplexer_2_out0), .out1(demultiplexer_2_out1), .out3(demultiplexer_2_out3),
    .in(multiplexer_1_out), .sel(\Selector_de_función ), .en(1'b1));  // open: out2
  Multiplexer #(.select(2), .width(12)) multiplexer_3 (
    .in1(demultiplexer_2_out1), .in2(demultiplexer_1_out2), .in3(demultiplexer_1_out3),
    .out(multiplexer_3_out), .sel(\Selector_de_función ), .en(1'b1));  // open: in0
  complemento_a_base_2__12_bits Complemento_a_la_base (
    .in_1(multiplexer_3_out), .out_2(Complemento_a_la_base_out_2), .out_3(Complemento_a_la_base_out_3));
  Multiplexer #(.select(2), .width(12)) multiplexer_4 (
    .in0(demultiplexer_2_out0), .in3(demultiplexer_2_out3), .out(multiplexer_4_out),
    .sel(\Selector_de_función ), .en(1'b1));  // open: in1, in2
  Multiplexer #(.select(2), .width(12)) multiplexer_5 (
    .in0(demultiplexer_1_out0), .in3(Complemento_a_la_base_out_2), .out(multiplexer_5_out),
    .sel(\Selector_de_función ), .en(1'b1));  // open: in1, in2
  sumador_de_12_bits sumador_de_12_bits_1 (
    .entrada_A(multiplexer_4_out), .entrada_B(multiplexer_5_out), .out_3(sumador_de_12_bits_1_out_3),
    .Overflow(sumador_de_12_bits_1_overflow));
  Multiplexer #(.select(2), .width(12)) multiplexer_6 (
    .in0(sumador_de_12_bits_1_out_3), .in1(Complemento_a_la_base_out_2), .in2(Complemento_a_la_base_out_2),
    .in3(sumador_de_12_bits_1_out_3), .out(out_5[11:0]), .sel(\Selector_de_función ), .en(1'b1));
  Multiplexer #(.select(2)) multiplexer_7 (
    .in0(sumador_de_12_bits_1_overflow), .in1(Complemento_a_la_base_out_3),
    .in2(Complemento_a_la_base_out_3), .in3(sumador_de_12_bits_1_overflow), .out(out_5[12]),
    .sel(\Selector_de_función ), .en(1'b1));
endmodule

// CSC
module sumador_completo (
  input  a,
  input  b,
  input  c,
  output s__carreo,
  output r__resultado
);

  wire a_b_c_out, a_b_prime_c_prime_out, a_prime_b_c_prime_out, a_prime_b_prime_c_out, ab_out, ac_out,
       bc_out, not_1_out, not_2_out, not_3_out;

  not not_1 (not_1_out, a);
  not not_2 (not_2_out, b);
  not not_3 (not_3_out, c);
  or ab (ab_out, a, b);
  or bc (bc_out, b, c);
  or ac (ac_out, a, c);
  or a_b_c (a_b_c_out, a, b, c);
  or a_prime_b_c_prime (a_prime_b_c_prime_out, not_1_out, b, not_3_out);
  or a_b_prime_c_prime (a_b_prime_c_prime_out, a, not_2_out, not_3_out);
  or a_prime_b_prime_c (a_prime_b_prime_c_out, not_1_out, not_2_out, c);
  and and_1 (s__carreo, ab_out, bc_out, ac_out);
  and and_2 (r__resultado, a_b_c_out, a_prime_b_c_prime_out, a_b_prime_c_prime_out, a_prime_b_prime_c_out);
endmodule

module complemento_a_base_2__12_bits (
  input  [11:0] in_1,
  output [11:0] out_2,
  output out_3
);

  wire [11:0] not_1_out;

  not not_1 (not_1_out[0], in_1[0]);
  not not_2 (not_1_out[1], in_1[1]);
  not not_3 (not_1_out[2], in_1[2]);
  not not_4 (not_1_out[3], in_1[3]);
  not not_5 (not_1_out[4], in_1[4]);
  not not_6 (not_1_out[5], in_1[5]);
  not not_7 (not_1_out[6], in_1[6]);
  not not_8 (not_1_out[7], in_1[7]);
  not not_9 (not_1_out[8], in_1[8]);
  not not_10 (not_1_out[9], in_1[9]);
  not not_11 (not_1_out[10], in_1[10]);
  not not_12 (not_1_out[11], in_1[11]);
  sumador_de_12_bits sumador_de_12_bits_1 (.entrada_A(not_1_out), .entrada_B(12'h1), .out_3(out_2), .Overflow(out_3));
endmodule

module sumador_de_12_bits (
  input  [11:0] entrada_A,
  input  [11:0] entrada_B,
  output [11:0] out_3,
  output Overflow
);

  wire sumador_completo_1_s__carreo, sumador_completo_2_s__carreo, sumador_completo_3_s__carreo,
       sumador_completo_4_s__carreo, sumador_completo_5_s__carreo, sumador_completo_6_s__carreo,
       sumador_completo_7_s__carreo, sumador_completo_8_s__carreo, sumador_completo_9_s__carreo,
       sumador_completo_10_s__carreo, sumador_completo_11_s__carreo;

  sumador_completo sumador_completo_1 (
    .a(entrada_A[0]), .b(entrada_B[0]), .c(1'b0), .s__carreo(sumador_completo_1_s__carreo),
    .r__resultado(out_3[0]));
  sumador_completo sumador_completo_2 (
    .a(entrada_A[1]), .b(entrada_B[1]), .c(sumador_completo_1_s__carreo),
    .s__carreo(sumador_completo_2_s__carreo), .r__resultado(out_3[1]));
  sumador_completo sumador_completo_3 (
    .a(entrada_A[2]), .b(entrada_B[2]), .c(sumador_completo_2_s__carreo),
    .s__carreo(sumador_completo_3_s__carreo), .r__resultado(out_3[2]));
  sumador_completo sumador_completo_4 (
    .a(entrada_A[3]), .b(entrada_B[3]), .c(sumador_completo_3_s__carreo),
    .s__carreo(sumador_completo_4_s__carreo), .r__resultado(out_3[3]));
  sumador_completo sumador_completo_5 (
    .a(entrada_A[4]), .b(entrada_B[4]), .c(sumador_completo_4_s__carreo),
    .s__carreo(sumador_completo_5_s__carreo), .r__resultado(out_3[4]));
  sumador_completo Sumador_completo_de_dos_bits ();  // open: a, b, c, s__carreo, r__resultado
  sumador_completo sumador_completo_6 (
    .a(entrada_A[5]), .b(entrada_B[5]), .c(sumador_completo_5_s__carreo),
    .s__carreo(sumador_completo_6_s__carreo), .r__resultado(out_3[5]));
  sumador_completo sumador_completo_7 (
    .a(entrada_A[6]), .b(entrada_B[6]), .c(sumador_completo_6_s__carreo),
    .s__carreo(sumador_completo_7_s__carreo), .r__resultado(out_3[6]));
  sumador_completo sumador_completo_8 (
    .a(entrada_A[7]), .b(entrada_B[7]), .c(sumador_completo_7_s__carreo),
    .s__carreo(sumador_completo_8_s__carreo), .r__resultado(out_3[7]));
  sumador_completo sumador_completo_9 (
    .a(entrada_A[8]), .b(entrada_B[8]), .c(sumador_completo_8_s__carreo),
    .s__carreo(sumador_completo_9_s__carreo), .r__resultado(out_3[8]));
  sumador_completo sumador_completo_10 (
    .a(entrada_A[9]), .b(entrada_B[9]), .c(sumador_completo_9_s__carreo),
    .s__carreo(sumador_completo_10_s__carreo), .r__resultado(out_3[9]));
  sumador_completo sumador_completo_11 (
    .a(entrada_A[10]), .b(entrada_B[10]), .c(sumador_completo_10_s__carreo),
    .s__carreo(sumador_completo_11_s__carreo), .r__resultado(out_3[10]));
  sumador_completo sumador_completo_12 (
    .a(entrada_A[11]), .b(entrada_B[11]), .c(sumador_completo_11_s__carreo), .s__carreo(Overflow),
    .r__resultado(out_3[11]));

  // Notes on the sheet:
  //   carreo 
  //   carreo 
  //   resultado
endmodule

module Sol_parte_1 (
  input  in_1,
  input  [11:0] in_2,
  input  in_3,
  input  [11:0] in_4,
  output [11:0] out_5,
  output Overflow_de_la_suma
);

  wire not_1_out, not_2_out;
  wire [11:0] Complemento_a_la_base_2_out_2, Complemento_a_la_base_out_2, controlled_buffer_1_out,
       controlled_buffer_2_out;

  not not_1 (not_1_out, in_1);
  assign controlled_buffer_1_out = not_1_out ? in_2 : 12'bz;  // Controlled_Buffer controlled_buffer_1
  not not_2 (not_2_out, in_3);
  assign controlled_buffer_2_out = not_2_out ? in_4 : 12'bz;  // Controlled_Buffer controlled_buffer_2
  complemento_a_base_2__12_bits Complemento_a_la_base (
    .in_1(in_2), .out_2(Complemento_a_la_base_out_2));  // open: out_3
  complemento_a_base_2__12_bits Complemento_a_la_base_2 (
    .in_1(in_4), .out_2(Complemento_a_la_base_2_out_2));  // open: out_3
  assign controlled_buffer_1_out = in_1 ? Complemento_a_la_base_out_2 : 12'bz;  // Controlled_Buffer controlled_buffer_3
  assign controlled_buffer_2_out = in_3 ? Complemento_a_la_base_2_out_2 : 12'bz;  // Controlled_Buffer controlled_buffer_4
  sumador_de_12_bits Sumador_12_bits (
    .entrada_A(controlled_buffer_1_out), .entrada_B(controlled_buffer_2_out), .out_3(out_5),
    .Overflow(Overflow_de_la_suma));
endmodule

module comparador (
  input  [11:0] in_1,
  input  [11:0] in_2,
  output A__B,
  output A__B_2,
  output A_B
);

  wire controlled_buffer_2_out, todos_seros_out;
  wire [11:0] complemento_a_base_2_12_bits_1_out_2, sumador_de_12_bits_1_out_3;

  complemento_a_base_2__12_bits complemento_a_base_2_12_bits_1 (
    .in_1(in_2), .out_2(complemento_a_base_2_12_bits_1_out_2));  // open: out_3
  sumador_de_12_bits sumador_de_12_bits_1 (
    .entrada_A(in_1), .entrada_B(complemento_a_base_2_12_bits_1_out_2), .out_3(sumador_de_12_bits_1_out_3));  // open: Overflow
  or todos_seros (todos_seros_out, sumador_de_12_bits_1_out_3[0], sumador_de_12_bits_1_out_3[1], sumador_de_12_bits_1_out_3[2], sumador_de_12_bits_1_out_3[3], sumador_de_12_bits_1_out_3[4], sumador_de_12_bits_1_out_3[5], sumador_de_12_bits_1_out_3[6], sumador_de_12_bits_1_out_3[7], sumador_de_12_bits_1_out_3[8], sumador_de_12_bits_1_out_3[9], sumador_de_12_bits_1_out_3[10], sumador_de_12_bits_1_out_3[11]);
  assign A__B_2 = todos_seros_out ? sumador_de_12_bits_1_out_3[11] : 1'bz;  // Controlled_Buffer controlled_buffer_1
  assign controlled_buffer_2_out = todos_seros_out ? sumador_de_12_bits_1_out_3[11] : 1'bz;  // Controlled_Buffer controlled_buffer_2
  not not_1 (A__B, todos_seros_out);
  not not_2 (A_B, controlled_buffer_2_out);
endmodule

module circuito_parte_2 (
  input  [11:0] in_1,
  input  [1:0] \Selector_de_función ,
  input  Invertir_entradas,
  input  [11:0] in_4,
  output [12:0] out_5
);

  wire Complemento_a_la_base_out_3, sumador_de_12_bits_1_overflow;
  wire [11:0] Complemento_a_la_base_out_2, demultiplexer_1_out0, demultiplexer_1_out2, demultiplexer_1_out3,
       demultiplexer_2_out0, demultiplexer_2_out1, demultiplexer_2_out3, multiplexer_1_out,
       multiplexer_2_out, multiplexer_3_out, multiplexer_4_out, multiplexer_5_out, sumador_de_12_bits_1_out_3;

  Multiplexer #(.width(12)) multiplexer_1 (
    .in0(in_1), .in1(in_4), .out(multiplexer_1_out), .sel(Invertir_entradas), .en(1'b1));
  Demultiplexer #(.select(2), .width(12)) demultiplexer_1 (
    .out0(demultiplexer_1_out0), .out2(demultiplexer_1_out2), .out3(demultiplexer_1_out3),
    .in(multiplexer_2_out), .sel(\Selector_de_función ), .en(1'b1));  // open: out1
  Multiplexer #(.width(12)) multiplexer_2 (
    .in0(in_4), .in1(in_1), .out(multiplexer_2_out), .sel(Invertir_entradas), .en(1'b1));
  Demultiplexer #(.select(2), .width(12)) demultiplexer_2 (
    .out0(demultiplexer_2_out0), .out1(demultiplexer_2_out1), .out3(demultiplexer_2_out3),
    .in(multiplexer_1_out), .sel(\Selector_de_función ), .en(1'b1));  // open: out2
  complemento_a_base_2__12_bits Complemento_a_la_base (
    .in_1(multiplexer_3_out), .out_2(Complemento_a_la_base_out_2), .out_3(Complemento_a_la_base_out_3));
  Multiplexer #(.select(2), .width(12)) multiplexer_3 (
    .in1(demultiplexer_2_out1), .in2(demultiplexer_1_out2), .in3(demultiplexer_1_out3),
    .out(multiplexer_3_out), .sel(\Selector_de_función ), .en(1'b1));  // open: in0
  Multiplexer #(.select(2), .width(12)) multiplexer_4 (
    .in0(demultiplexer_2_out0), .in3(demultiplexer_2_out3), .out(multiplexer_4_out),
    .sel(\Selector_de_función ), .en(1'b1));  // open: in1, in2
  Multiplexer #(.select(2), .width(12)) multiplexer_5 (
    .in0(demultiplexer_1_out0), .in3(Complemento_a_la_base_out_2), .out(multiplexer_5_out),
    .sel(\Selector_de_función ), .en(1'b1));  // open: in1, in2
  sumador_de_12_bits sumador_de_12_bits_1 (
    .entrada_A(multiplexer_4_out), .entrada_B(multiplexer_5_out), .out_3(sumador_de_12_bits_1_out_3),
    .Overflow(sumador_de_12_bits_1_overflow));
  Multiplexer #(.select(2), .width(12)) multiplexer_6 (
    .in0(sumador_de_12_bits_1_out_3), .in1(Complemento_a_la_base_out_2), .in2(Complemento_a_la_base_out_2),
    .in3(sumador_de_12_bits_1_out_3), .out(out_5[11:0]), .sel(\Selector_de_función ), .en(1'b1));
  Multiplexer #(.select(2)) multiplexer_7 (
    .in0(sumador_de_12_bits_1_overflow), .in1(Complemento_a_la_base_out_3),
    .in2(Complemento_a_la_base_out_3), .in3(sumador_de_12_bits_1_overflow), .out(out_5[12]),
    .sel(\Selector_de_función ), .en(1'b1));
endmodule

module circuito_final (
  input  [11:0] in_1,
  input  [2:0] \Selector_de_función ,
  input  Invertir_entradas,
  input  [11:0] in_4,
  output [12:0] out_5
);

  wire comparador_1_a__b, comparador_1_a__b_2, comparador_1_a_b, Complemento_a_la_base_out_3,
       sumador_de_12_bits_1_overflow;
  wire [11:0] Complemento_a_la_base_out_2, demultiplexer_1_out0, demultiplexer_1_out2, demultiplexer_1_out3,
       demultiplexer_1_out6, demultiplexer_2_out0, demultiplexer_2_out1, demultiplexer_2_out3,
       multiplexer_1_out, multiplexer_2_out, multiplexer_3_out, multiplexer_4_out, multiplexer_5_out,
       sumador_de_12_bits_1_out_3;

  Multiplexer #(.width(12)) multiplexer_1 (
    .in0(in_1), .in1(in_4), .out(multiplexer_1_out), .sel(Invertir_entradas), .en(1'b1));
  Multiplexer #(.width(12)) multiplexer_2 (
    .in0(in_4), .in1(in_1), .out(multiplexer_2_out), .sel(Invertir_entradas), .en(1'b1));
  Demultiplexer #(.select(3), .width(12)) demultiplexer_1 (
    .out0(demultiplexer_1_out0), .out2(demultiplexer_1_out2), .out3(demultiplexer_1_out3),
    .out6(demultiplexer_1_out6), .in(multiplexer_2_out), .sel(\Selector_de_función ), .en(1'b1));  // open: out1, out4, out5, out7
  Demultiplexer #(.select(3), .width(12)) demultiplexer_2 (
    .out0(demultiplexer_2_out0), .out1(demultiplexer_2_out1), .out3(demultiplexer_2_out3),
    .out6(demultiplexer_1_out3), .in(multiplexer_1_out), .sel(\Selector_de_función ), .en(1'b1));  // open: out2, out4, out5, out7
  complemento_a_base_2__12_bits Complemento_a_la_base (
    .in_1(multiplexer_3_out), .out_2(Complemento_a_la_base_out_2), .out_3(Complemento_a_la_base_out_3));
  Multiplexer #(.select(3), .width(12)) multiplexer_3 (
    .in1(demultiplexer_2_out1), .in2(demultiplexer_1_out2), .in3(demultiplexer_1_out3),
    .out(multiplexer_3_out), .sel(\Selector_de_función ), .en(1'b1));  // open: in0, in4, in5, in6, in7
  Multiplexer #(.select(3), .width(12)) multiplexer_4 (
    .in0(demultiplexer_2_out0), .in3(demultiplexer_2_out3), .out(multiplexer_4_out),
    .sel(\Selector_de_función ), .en(1'b1));  // open: in1, in2, in4, in5, in6, in7
  Multiplexer #(.select(3), .width(12)) multiplexer_5 (
    .in0(demultiplexer_1_out0), .in3(Complemento_a_la_base_out_2), .out(multiplexer_5_out),
    .sel(\Selector_de_función ), .en(1'b1));  // open: in1, in2, in4, in5, in6, in7
  sumador_de_12_bits sumador_de_12_bits_1 (
    .entrada_A(multiplexer_4_out), .entrada_B(multiplexer_5_out), .out_3(sumador_de_12_bits_1_out_3),
    .Overflow(sumador_de_12_bits_1_overflow));
  Multiplexer #(.select(3), .width(12)) multiplexer_6 (
    .in0(sumador_de_12_bits_1_out_3), .in1(Complemento_a_la_base_out_2), .in2(Complemento_a_la_base_out_2),
    .in3(sumador_de_12_bits_1_out_3), .out(out_5[11:0]), .sel(\Selector_de_función ), .en(1'b1));  // open: in4, in5, in6, in7
  LED led_1 (.in(comparador_1_a_b));
  comparador comparador_1 (
    .in_1(demultiplexer_1_out3), .in_2(demultiplexer_1_out6), .A__B(comparador_1_a__b),
    .A__B_2(comparador_1_a__b_2), .A_B(comparador_1_a_b));
  LED led_2 (.in(comparador_1_a__b_2));
  LED led_3 (.in(comparador_1_a__b));
  Multiplexer #(.select(3)) multiplexer_7 (
    .in0(sumador_de_12_bits_1_overflow), .in1(Complemento_a_la_base_out_3),
    .in2(Complemento_a_la_base_out_3), .in3(sumador_de_12_bits_1_overflow), .out(out_5[12]),
    .sel(\Selector_de_función ), .en(1'b1));  // open: in4, in5, in6, in7
endmodule

module divisor (
  input  in_1,
  input  [11:0] in_2,
  input  [11:0] in_3,
  output [11:0] out_4
);

  wire clock_1_out, comparador_1_a_b, controlled_inverter_1_out, not_1_out, not_2_out, not_3_out;
  wire [11:0] controlled_buffer_2_out, controlled_inverter_2_out, controlled_inverter_3_out,
       sumador_de_12_bits_1_out_3, undriven;

  Clock clock_1 (.out(clock_1_out));
  complemento_a_base_2__12_bits complemento_a_base_2_12_bits_1 (.in_1(in_3));  // open: out_2, out_3
  assign controlled_inverter_1_out = not_1_out ? ~clock_1_out : 1'bz;  // Controlled_Inverter controlled_inverter_1
  assign controlled_inverter_2_out = in_1 ? ~in_2 : 12'bz;  // Controlled_Inverter controlled_inverter_2
  assign controlled_inverter_2_out = controlled_inverter_1_out ? controlled_buffer_2_out : 12'bz;  // Controlled_Buffer controlled_buffer_1
  not not_1 (not_1_out, comparador_1_a_b);
  not not_2 (not_2_out, controlled_inverter_1_out);
  sumador_de_12_bits sumador_de_12_bits_1 (
    .entrada_A(controlled_inverter_2_out), .entrada_B(undriven), .out_3(sumador_de_12_bits_1_out_3));  // open: Overflow
  assign controlled_buffer_2_out = not_2_out ? sumador_de_12_bits_1_out_3 : 12'bz;  // Controlled_Buffer controlled_buffer_2
  sumador_de_12_bits sumador_de_12_bits_2 (
    .entrada_A(controlled_buffer_2_out), .entrada_B(undriven), .out_3(controlled_buffer_2_out));  // open: Overflow
  not not_3 (not_3_out, controlled_inverter_1_out);
  assign controlled_inverter_3_out = controlled_inverter_1_out ? ~sumador_de_12_bits_1_out_3 : 12'bz;  // Controlled_Inverter controlled_inverter_3
  assign controlled_inverter_3_out = not_3_out ? ~controlled_buffer_2_out : 12'bz;  // Controlled_Inverter controlled_inverter_4
  comparador comparador_1 (
    .in_1(controlled_inverter_3_out), .in_2(in_3), .A_B(comparador_1_a_b));  // open: A__B, A__B_2
  assign out_4 = comparador_1_a_b ? controlled_inverter_3_out : 12'bz;  // Controlled_Buffer controlled_buffer_3
endmodule
